// Logisim project MIPS8bits_PIPELINE_hazard.circ as structural Verilog: 5 circuits, main circuit Mini-Mips-8bits
module Mini_Mips_8bits (
  input  IncPc,
  input  Clear,
  input  EscReg,
  input  ClearReg,
  input  RegDst,
  input  UlaFonte,
  input  [2:0] ControleULA,
  input  EscMem,
  input  ClearData,
  input  MemParaReg,
  output [3:0] OPCODE,
  output [7:0] SaidaULA,
  output [7:0] Entrada_B_Reg,
  output [7:0] Op1,
  output out_15,
  output [7:0] Op2,
  output [7:0] \Endereço ,
  output [7:0] Data,
  output [15:0] \Instrução 
);

  wire clk, not_1_out;
  wire [2:0] multiplexer_1_out;
  wire [7:0] ram_1_data;

  Clock u_Clk (.out(clk));
  \Busca_Instrução  \busca_instrução_1  (.Enable(IncPc), .Clock(clk), .Clear(Clear), .PC(\Endereço ));
  Hex_Digit_Display hex_digit_display_1 (.value(\Endereço [7:4]), .dp(1'b1));
  Hex_Digit_Display hex_digit_display_2 (.value(\Endereço [3:0]), .dp(1'b1));
  ROM #(.dataWidth(16)) rom_1 (.addr(\Endereço ), .data(\Instrução ));  // open: sel
  Banco_registradores_Mini_Mips8Bits_sMux banco_registradores_mini_mips8bits_smux_1 (
    .Read_Register_1(\Instrução [11:9]), .Read_Register_2(\Instrução [8:6]), .Write_data(Entrada_B_Reg),
    .RegWrite(EscReg), .Write_Register(multiplexer_1_out), .Clock(clk), .Clear(ClearReg), .Read_data_1(Op1),
    .Read_data_2(Data));
  Multiplexer #(.width(3), .enable("false")) multiplexer_1 (
    .in0(\Instrução [8:6]), .in1(\Instrução [5:3]), .out(multiplexer_1_out), .sel(RegDst));
  Multiplexer #(.width(8), .enable("false")) multiplexer_2 (
    .in0(Data), .in1({{3{\Instrução [5]}}, \Instrução [4:0]}), .out(Op2), .sel(UlaFonte));
  ULA ula_1 (.Flag(out_15), .resultado(SaidaULA), .in_1(ControleULA), .in_2(Op1), .in_3(Op2));
  not not_1 (not_1_out, EscMem);
  RAM #(.bus("separate")) ram_1 (
    .addr(SaidaULA), .din(Data), .data(ram_1_data), .str(EscMem), .clk(clk), .ld(not_1_out), .clr(ClearData));  // open: sel
  Multiplexer #(.width(8), .enable("false")) multiplexer_3 (
    .in0(ram_1_data), .in1(SaidaULA), .out(Entrada_B_Reg), .sel(MemParaReg));

  assign OPCODE = \Instrução [15:12];

  // Notes on the sheet:
  //   RegDst: pull=up
  //   Clear: pull=down
  //   Instrução: pull=down
  //   UlaFonte: pull=up
  //   IncPc: pull=down
  //   ClearData: pull=down
  //   MemParaReg: pull=up
  //   OPCODE: pull=down
  //   ControleULA: pull=up
  //   EscReg: pull=up
  //   ClearReg: pull=down
  //   EscMem: pull=up
  //   Endereço: pull=down
  //   contents of rom_1 (hex, n*v repeats v):
  //   b08a b0cb 4041 20 8603 520 65a 2004 f10c
endmodule

// RegDst
module Mini_MIPS_8bits_Controle (
  input  ClearReg,
  input  Clear,
  input  ClearData,
  output [3:0] OPCODE,
  output [7:0] SaidaULA,
  output [7:0] Entrada_B_Reg,
  output [7:0] Op1,
  output out_8,
  output [7:0] Op2,
  output [7:0] \Endereço ,
  output [7:0] Data,
  output [15:0] \Instrução ,
  output [2:0] ControleUla,
  output RegDst,
  output EscMem,
  output MemParaReg,
  output UlaFonte
);

  wire clk, EscReg, IncPc, not_1_out;
  wire [2:0] multiplexer_1_out;
  wire [7:0] ram_1_data;

  Clock u_Clk (.out(clk));
  \Busca_Instrução  \busca_instrução_1  (.Enable(IncPc), .Clock(clk), .Clear(Clear), .PC(\Endereço ));
  Hex_Digit_Display hex_digit_display_1 (.value(\Endereço [7:4]), .dp(1'b1));
  Hex_Digit_Display hex_digit_display_2 (.value(\Endereço [3:0]), .dp(1'b1));
  ControleMiniMips controleminimips_1 (
    .OP3(\Instrução [15]), .OP2(\Instrução [14]), .OP1(\Instrução [13]), .OP0(\Instrução [12]),
    .Funct2(\Instrução [2]), .IncPC(IncPc), .Funct1(\Instrução [1]), .RegDst(RegDst),
    .Funct0(\Instrução [0]), .UlaFonte(UlaFonte), .MemParaReg(MemParaReg), .EscReg(EscReg), .EscMem(EscMem),
    .ControleUla2(ControleUla[2]), .ControleUla1(ControleUla[1]), .ControleUla0(ControleUla[0]));  // open: Branch, Jump
  ROM #(.dataWidth(16)) rom_1 (.addr(\Endereço ), .data(\Instrução ));  // open: sel
  Banco_registradores_Mini_Mips8Bits_sMux banco_registradores_mini_mips8bits_smux_1 (
    .Read_Register_1(\Instrução [11:9]), .Read_Register_2(\Instrução [8:6]), .Write_data(Entrada_B_Reg),
    .RegWrite(EscReg), .Write_Register(multiplexer_1_out), .Clock(clk), .Clear(ClearReg), .Read_data_1(Op1),
    .Read_data_2(Data));
  Multiplexer #(.width(3), .enable("false")) multiplexer_1 (
    .in0(\Instrução [8:6]), .in1(\Instrução [5:3]), .out(multiplexer_1_out), .sel(RegDst));
  Multiplexer #(.width(8), .enable("false")) multiplexer_2 (
    .in0(Data), .in1({{3{\Instrução [5]}}, \Instrução [4:0]}), .out(Op2), .sel(UlaFonte));
  ULA ula_1 (.Flag(out_8), .resultado(SaidaULA), .in_1(ControleUla), .in_2(Op1), .in_3(Op2));
  not not_1 (not_1_out, EscMem);
  RAM #(.bus("separate")) ram_1 (
    .addr(SaidaULA), .din(Data), .data(ram_1_data), .str(EscMem), .clk(clk), .ld(not_1_out), .clr(ClearData));  // open: sel
  Multiplexer #(.width(8), .enable("false")) multiplexer_3 (
    .in0(ram_1_data), .in1(SaidaULA), .out(Entrada_B_Reg), .sel(MemParaReg));

  assign OPCODE = \Instrução [15:12];

  // Other names for the same wires on the sheet: Funct[2:0] = \Instrução [2:0]

  // Notes on the sheet:
  //   EscMem: pull=down
  //   Endereço: pull=down
  //   MemParaReg: pull=down
  //   UlaFonte: pull=down
  //   ClearData: pull=down
  //   ClearReg: pull=down
  //   Instrução: pull=down
  //   ControleUla: pull=down
  //   RegDst: pull=down
  //   OPCODE: pull=down
  //   Clear: pull=down
  //   contents of rom_1 (hex, n*v repeats v):
  //   0 4085 4043 458 410a f080 f104 b044 8088 8141 868a 2001
endmodule

module Mini_MIPS_Controle_Jump_Branch (
  input  Clear,
  input  ClearReg,
  input  ClearData,
  output [3:0] OPCODE,
  output [7:0] SaidaULA,
  output [7:0] Entrada_B_Reg,
  output [7:0] Op1,
  output out_8,
  output [7:0] Op2,
  output [7:0] \Endereço ,
  output [7:0] Data,
  output [15:0] \Instrução ,
  output [2:0] ControleUla,
  output [7:0] PC_Branch,
  output [7:0] PC_Jump,
  output RegDst,
  output EscMem,
  output MemParaReg,
  output UlaFonte
);

  wire Branch, clk, controleminimips_1_branch, EscReg, IncPc, Jump, not_1_out;
  wire [2:0] multiplexer_3_out;
  wire [7:0] multiplexer_1_out, multiplexer_2_out, PC_1, ram_1_data;

  Clock u_Clk (.out(clk));
  Multiplexer #(.width(8), .enable("false")) multiplexer_1 (
    .in0(PC_1), .in1(PC_Branch), .out(multiplexer_1_out), .sel(Branch));
  Multiplexer #(.width(8), .enable("false")) multiplexer_2 (
    .in0(multiplexer_1_out), .in1(\Instrução [7:0]), .out(multiplexer_2_out), .sel(Jump));
  Register PC (.D(multiplexer_2_out), .en(IncPc), .Q(\Endereço ), .clk(clk), .clr(Clear));
  Adder adder_1 (.a(8'h1), .b(\Endereço ), .out(PC_1));  // open: cin, cout
  ControleMiniMips controleminimips_1 (
    .OP3(\Instrução [15]), .Branch(controleminimips_1_branch), .OP2(\Instrução [14]), .OP1(\Instrução [13]),
    .Jump(Jump), .OP0(\Instrução [12]), .Funct2(\Instrução [2]), .IncPC(IncPc), .Funct1(\Instrução [1]),
    .RegDst(RegDst), .Funct0(\Instrução [0]), .UlaFonte(UlaFonte), .MemParaReg(MemParaReg), .EscReg(EscReg),
    .EscMem(EscMem), .ControleUla2(ControleUla[2]), .ControleUla1(ControleUla[1]),
    .ControleUla0(ControleUla[0]));
  ROM #(.dataWidth(16)) rom_1 (.addr(\Endereço ), .data(\Instrução ));  // open: sel
  and and_1 (Branch, out_8, controleminimips_1_branch);
  Multiplexer #(.width(3), .enable("false")) multiplexer_3 (
    .in0(\Instrução [8:6]), .in1(\Instrução [5:3]), .out(multiplexer_3_out), .sel(RegDst));
  Banco_registradores_Mini_Mips8Bits_sMux banco_registradores_mini_mips8bits_smux_1 (
    .Read_Register_1(\Instrução [11:9]), .Read_Register_2(\Instrução [8:6]), .Write_data(Entrada_B_Reg),
    .RegWrite(EscReg), .Write_Register(multiplexer_3_out), .Clock(clk), .Clear(ClearReg), .Read_data_1(Op1),
    .Read_data_2(Data));
  Multiplexer #(.width(8), .enable("false")) multiplexer_4 (
    .in0(Data), .in1({{3{\Instrução [5]}}, \Instrução [4:0]}), .out(Op2), .sel(UlaFonte));
  ULA ula_1 (.Flag(out_8), .resultado(SaidaULA), .in_1(ControleUla), .in_2(Op1), .in_3(Op2));
  Adder adder_2 (.a({{3{\Instrução [5]}}, \Instrução [4:0]}), .b(PC_1), .out(PC_Branch));  // open: cin, cout
  RAM #(.bus("separate")) ram_1 (
    .addr(SaidaULA), .din(Data), .data(ram_1_data), .str(EscMem), .clk(clk), .ld(not_1_out), .clr(ClearData));  // open: sel
  not not_1 (not_1_out, EscMem);
  Multiplexer #(.width(8), .enable("false")) multiplexer_5 (
    .in0(ram_1_data), .in1(SaidaULA), .out(Entrada_B_Reg), .sel(MemParaReg));

  assign OPCODE = \Instrução [15:12];
  assign PC_Jump = \Instrução [7:0];

  // Other names for the same wires on the sheet: Funct[2:0] = \Instrução [2:0]; ZeroUla = out_8

  // Notes on the sheet:
  //   RegDst: pull=down
  //   ClearReg: pull=down
  //   EscMem: pull=down
  //   ControleUla: pull=down
  //   MemParaReg: pull=down
  //   Endereço: pull=down
  //   UlaFonte: pull=down
  //   ClearData: pull=down
  //   Clear: pull=down
  //   OPCODE: pull=down
  //   Instrução: pull=down
  //   contents of rom_1 (hex, n*v repeats v):
  //   4085 4043 458 410a f080 f104 b044 8088 8141 868a 2000
endmodule

module Mini_MIPS_Controle_Multiciclo (
  input  ClearData,
  input  in_2,
  output [3:0] OPCODE,
  output [7:0] Op1,
  output out_5,
  output [7:0] \Endereço ,
  output [7:0] SaidaULA,
  output [15:0] \Instrução ,
  output [7:0] Op2,
  output [7:0] Valor_IMM,
  output [7:0] Dados_para_Reg,
  output [1:0] PCFonte,
  output [2:0] ControleUla,
  output MemParaReg,
  output RegDst,
  output [1:0] UlaFonteB,
  output UlaFonteA,
  output [2:0] Funct,
  output [3:0] OPCODE_2,
  output [1:0] out_20,
  output [1:0] out_21,
  output [2:0] out_22
);

  wire and_1_out, Branch, Clk, EscMem, EscReg, IouD, IREsc, not_1_out, PC, PCEsc;
  wire [2:0] multiplexer_2_out;
  wire [3:0] controle_multiciclo_1_e0;
  wire [7:0] A_q, B_q, banco_registradores_mini_mips8bits_smux_1_read_data_1,
       banco_registradores_mini_mips8bits_smux_1_read_data_2, multiplexer_6_out, PC_q, ULA_saida_q, undriven;
  wire [7:6] RI_q_2;
  wire [11:8] RI_q;
  wire [15:0] RDM_q;

  Register u_PC (.D(multiplexer_6_out), .en(PC), .Q(PC_q), .clk(Clk), .clr(in_2));
  Hex_Digit_Display hex_digit_display_1 (.value(controle_multiciclo_1_e0));  // open: dp
  Multiplexer #(.width(8), .enable("false")) multiplexer_1 (
    .in0(PC_q), .in1(ULA_saida_q), .out(\Endereço ), .sel(IouD));
  Clock u_Clk (.out(Clk));
  RAM #(.dataWidth(16), .bus("separate")) ram_1 (
    .addr(\Endereço ), .din({{8{1'b0}}, B_q}), .data(\Instrução ), .str(EscMem), .clk(Clk), .ld(not_1_out),
    .clr(ClearData));  // open: sel
  not not_1 (not_1_out, EscMem);
  Register #(.width(16)) RI (
    .D(\Instrução ), .en(IREsc), .Q({OPCODE, RI_q, RI_q_2, Valor_IMM[7], Valor_IMM[4:3], Funct}), .clk(Clk),
    .clr(in_2));
  Register #(.width(16)) RDM (.D(\Instrução ), .Q(RDM_q), .clk(Clk), .clr(in_2));  // open: en
  Controle_Multiciclo controle_multiciclo_1 (
    .Op3(OPCODE[3]), .Op2(OPCODE[2]), .Op1(OPCODE[1]), .Op0(OPCODE[0]), .Funct2(Funct[2]), .Funct1(Funct[1]),
    .Funct0(Funct[0]), .Clock(Clk), .Clear(in_2), .ControleUla2(ControleUla[2]), .Branch(Branch),
    .ControleUla1(ControleUla[1]), .PCEsc(PCEsc), .ControleUla0(ControleUla[0]), .IouD(IouD),
    .EscMem(EscMem), .IREsc(IREsc), .MemParaReg(MemParaReg), .RegDst(RegDst), .EscReg(EscReg),
    .UlaFonteA(UlaFonteA), .UlaFonteB1(out_21[1]), .UlaFonteB0(out_21[0]), .PCFonte1(out_20[1]),
    .PCFonte0(out_20[0]), .E3(controle_multiciclo_1_e0[3]), .E2(controle_multiciclo_1_e0[2]),
    .E1(controle_multiciclo_1_e0[1]), .E0(controle_multiciclo_1_e0[0]));
  Multiplexer #(.width(3), .enable("false")) multiplexer_2 (
    .in0({RI_q[8], RI_q_2}), .in1({Valor_IMM[7], Valor_IMM[4:3]}), .out(multiplexer_2_out), .sel(RegDst));
  Multiplexer #(.width(8), .enable("false")) multiplexer_3 (
    .in0(ULA_saida_q), .in1(RDM_q[7:0]), .out(Dados_para_Reg), .sel(MemParaReg));
  Banco_registradores_Mini_Mips8Bits_sMux banco_registradores_mini_mips8bits_smux_1 (
    .Read_Register_1(RI_q[11:9]), .Read_Register_2({RI_q[8], RI_q_2}), .Write_data(Dados_para_Reg),
    .RegWrite(EscReg), .Write_Register(multiplexer_2_out), .Clock(Clk), .Clear(in_2),
    .Read_data_1(banco_registradores_mini_mips8bits_smux_1_read_data_1),
    .Read_data_2(banco_registradores_mini_mips8bits_smux_1_read_data_2));
  Register A (.D(banco_registradores_mini_mips8bits_smux_1_read_data_1), .Q(A_q), .clk(Clk), .clr(in_2));  // open: en
  Register B (.D(banco_registradores_mini_mips8bits_smux_1_read_data_2), .Q(B_q), .clk(Clk), .clr(in_2));  // open: en
  and and_1 (and_1_out, out_5, Branch);
  or or_1 (PC, and_1_out, PCEsc);
  Multiplexer #(.width(8), .enable("false")) multiplexer_4 (.in0(PC_q), .in1(A_q), .out(Op1), .sel(UlaFonteA));
  Multiplexer #(.select(2), .width(8), .enable("false")) multiplexer_5 (
    .in0(B_q), .in1(8'h1), .in2({{3{Valor_IMM[7]}}, Valor_IMM[4:3], Funct}), .out(Op2), .sel(out_21));  // open: in3
  ULA ula_1 (.Flag(out_5), .resultado(SaidaULA), .in_1(ControleUla), .in_2(Op1), .in_3(Op2));
  Register ULA_saida (.D(SaidaULA), .Q(ULA_saida_q), .clk(Clk), .clr(in_2));  // open: en
  Multiplexer #(.select(2), .width(8), .enable("false")) multiplexer_6 (
    .in0(SaidaULA), .in1(ULA_saida_q), .in2({RI_q_2, Valor_IMM[7], Valor_IMM[4:3], Funct}), .in3(undriven),
    .out(multiplexer_6_out), .sel(out_20));

  assign OPCODE_2 = OPCODE;
  assign out_22 = ControleUla;
  assign PCFonte = out_20;
  assign UlaFonteB = out_21;
  assign {Valor_IMM[6:5], Valor_IMM[2:0]} = {{2{Valor_IMM[7]}}, Funct};

  // Other names for the same wires on the sheet: Clear = in_2; ZeroUla = out_5

  // Notes on the sheet:
  //   MemParaReg: pull=down
  //   out_21: pull=down
  //   out_20: pull=down
  //   ControleUla: pull=down
  //   UlaFonteB: pull=down
  //   OPCODE_2: pull=down
  //   ClearData: pull=down
  //   OPCODE: pull=down
  //   in_2: pull=down
  //   PCFonte: pull=down
  //   out_22: pull=down
  //   Valor_IMM: pull=down
  //   Dados_para_Reg: pull=down
  //   Endereço: pull=down
  //   UlaFonteA: pull=down
  //   RegDst: pull=down
  //   Instrução: pull=down
  //   Funct: pull=down
endmodule

module Mini_MIPS_PIPELINE (
  input  ClearReg,
  input  Clear,
  input  ClearData,
  output [2:0] Funct,
  output [3:0] OPCODE,
  output [7:0] SaidaULA,
  output [7:0] Entrada_B_Reg,
  output [7:0] Op1,
  output out_9,
  output [7:0] Op2,
  output [7:0] \Endereço ,
  output [15:0] \Instrução ,
  output [7:0] Data,
  output [7:0] PC_Branch,
  output [7:0] PC_Jump,
  output UlaFonte,
  output [2:0] ControleUla,
  output EscMem,
  output MemParaReg,
  output RegDst
);

  wire B2, B3, Branch, clk, EscReg, IncPc, Jump, not_1_out, or_1_out;
  wire [0:0] MEM_2_q;
  wire [1:0] controleminimips_1_memparareg, ER_2_q, ER_q;
  wire [2:0] multiplexer_5_out, RD_2_q, RD_3_q, RD_q, RS_q;
  wire [2:1] controleminimips_1_jump, MEM_q;
  wire [2:2] RS;
  wire [3:0] OPCODE_2_q, OPCODE_q;
  wire [4:0] controleminimips_1_regdst;
  wire [7:0] adder_1_out, B_2_q, banco_registradores_mini_mips8bits_smux_1_read_data_1,
       banco_registradores_mini_mips8bits_smux_1_read_data_2, IMM_q, MEM_3_q, multiplexer_1_out,
       multiplexer_2_out, PC_1, PC_1_q, ram_1_data, ULASaida_2_q, ULASaida_q;
  wire [11:9] multiplexer_3_out;
  wire [15:0] RI_q;

  Clock u_Clk (.out(clk));
  Multiplexer #(.width(8), .enable("false")) multiplexer_1 (
    .in0(adder_1_out), .in1(PC_Branch), .out(multiplexer_1_out), .sel(Branch));
  Multiplexer #(.width(8), .enable("false")) multiplexer_2 (
    .in0(multiplexer_1_out), .in1({PC_Jump[7:3], Funct}), .out(multiplexer_2_out), .sel(Jump));
  Register PC (.D(multiplexer_2_out), .en(IncPc), .Q(\Endereço ), .clk(clk), .clr(Clear));
  Adder adder_1 (.a(8'h1), .b(\Endereço ), .out(adder_1_out));  // open: cin, cout
  ROM #(.dataWidth(16)) rom_1 (.addr(\Endereço ), .data(\Instrução ));  // open: sel
  Register PC_2 (.D(adder_1_out), .Q(PC_1), .clk(clk), .clr(Clear));  // open: en
  Register #(.width(16)) RI (.D(\Instrução ), .Q(RI_q), .clk(clk), .clr(Clear));  // open: en
  Multiplexer #(.width(16), .enable("false")) multiplexer_3 (
    .in0(RI_q), .in1({16{1'b0}}), .out({OPCODE, multiplexer_3_out, RS[2], PC_Jump[7:3], Funct}),
    .sel(or_1_out));
  or or_1 (or_1_out, 1'b0, B2);
  ControleMiniMips controleminimips_1 (
    .OP3(OPCODE[3]), .Branch(B3), .OP2(OPCODE[2]), .OP1(OPCODE[1]), .Jump(controleminimips_1_jump[1]),
    .OP0(OPCODE[0]), .Funct2(Funct[2]), .IncPC(IncPc), .Funct1(Funct[1]),
    .RegDst(controleminimips_1_regdst[0]), .Funct0(Funct[0]), .UlaFonte(controleminimips_1_regdst[1]),
    .MemParaReg(controleminimips_1_memparareg[0]), .EscReg(controleminimips_1_memparareg[1]),
    .EscMem(controleminimips_1_jump[2]), .ControleUla2(controleminimips_1_regdst[2]),
    .ControleUla1(controleminimips_1_regdst[3]), .ControleUla0(controleminimips_1_regdst[4]));
  Banco_registradores_Mini_Mips8Bits_sMux banco_registradores_mini_mips8bits_smux_1 (
    .Read_Register_1(multiplexer_3_out), .Read_Register_2({RS[2], PC_Jump[7:6]}), .Write_data(Entrada_B_Reg),
    .RegWrite(EscReg), .Write_Register(RD_3_q), .Clock(clk), .Clear(ClearReg),
    .Read_data_1(banco_registradores_mini_mips8bits_smux_1_read_data_1),
    .Read_data_2(banco_registradores_mini_mips8bits_smux_1_read_data_2));
  Register #(.width(2)) ER (.D(controleminimips_1_memparareg), .Q(ER_q), .clk(clk), .clr(Clear));  // open: en
  Register #(.width(3)) MEM (.D({controleminimips_1_jump, B3}), .Q({MEM_q, B2}), .clk(clk), .clr(Clear));  // open: en
  Register #(.width(5)) EX (
    .D(controleminimips_1_regdst), .Q({ControleUla[0], ControleUla[1], ControleUla[2], UlaFonte, RegDst}),
    .clk(clk), .clr(Clear));  // open: en
  Register #(.width(4)) u_OPCODE (.D(OPCODE), .Q(OPCODE_q), .clk(clk), .clr(Clear));  // open: en
  Register A (.D(banco_registradores_mini_mips8bits_smux_1_read_data_1), .Q(Op1), .clk(clk), .clr(Clear));  // open: en
  Register B (.D(banco_registradores_mini_mips8bits_smux_1_read_data_2), .Q(Data), .clk(clk), .clr(Clear));  // open: en
  Register IMM (.D({{3{PC_Jump[5]}}, PC_Jump[4:3], Funct}), .Q(IMM_q), .clk(clk), .clr(Clear));  // open: en
  Register u_PC_1 (.D(PC_1), .Q(PC_1_q), .clk(clk), .clr(Clear));  // open: en
  Register #(.width(3)) u_RS (.D({RS[2], PC_Jump[7:6]}), .Q(RS_q), .clk(clk), .clr(Clear));  // open: en
  Register #(.width(3)) RD (.D(PC_Jump[5:3]), .Q(RD_q), .clk(clk), .clr(Clear));  // open: en
  Multiplexer #(.width(8), .enable("false")) multiplexer_4 (.in0(Data), .in1(IMM_q), .out(Op2), .sel(UlaFonte));
  Adder adder_2 (.a(IMM_q), .b(PC_1_q), .out(PC_Branch));  // open: cin, cout
  Multiplexer #(.width(3), .enable("false")) multiplexer_5 (
    .in0(RS_q), .in1(RD_q), .out(multiplexer_5_out), .sel(RegDst));
  ULA ula_1 (.Flag(out_9), .resultado(SaidaULA), .in_1(ControleUla), .in_2(Op1), .in_3(Op2));
  Register #(.width(2)) ER_2 (.D(ER_q), .Q(ER_2_q), .clk(clk), .clr(Clear));  // open: en
  Register #(.width(3)) MEM_2 (.D({MEM_q, B2}), .Q({EscMem, Jump, MEM_2_q[0]}), .clk(clk), .clr(Clear));  // open: en
  Register #(.width(4)) OPCODE_2 (.D(OPCODE_q), .Q(OPCODE_2_q), .clk(clk), .clr(Clear));  // open: en
  Register ULASaida (.D(SaidaULA), .Q(ULASaida_q), .clk(clk), .clr(Clear));  // open: en
  Register B_2 (.D(Data), .Q(B_2_q), .clk(clk), .clr(Clear));  // open: en
  Register #(.width(3)) RD_2 (.D(multiplexer_5_out), .Q(RD_2_q), .clk(clk), .clr(Clear));  // open: en
  and and_1 (Branch, out_9, MEM_2_q[0]);
  not not_1 (not_1_out, EscMem);
  RAM #(.bus("separate")) ram_1 (
    .addr(ULASaida_q), .din(B_2_q), .data(ram_1_data), .str(EscMem), .clk(clk), .ld(not_1_out),
    .clr(ClearData));  // open: sel
  Register #(.width(2)) ER_3 (.D(ER_2_q), .Q({EscReg, MemParaReg}), .clk(clk));  // open: en, clr
  Register #(.width(4)) OPCODE_3 (.D(OPCODE_2_q), .clk(clk), .clr(Clear));  // open: en, Q
  Register MEM_3 (.D(ram_1_data), .Q(MEM_3_q), .clk(clk), .clr(Clear));  // open: en
  Register ULASaida_2 (.D(ULASaida_q), .Q(ULASaida_2_q), .clk(clk), .clr(Clear));  // open: en
  Register #(.width(3)) RD_3 (.D(RD_2_q), .Q(RD_3_q), .clk(clk), .clr(Clear));  // open: en
  Multiplexer #(.width(8), .enable("false")) multiplexer_6 (
    .in0(MEM_3_q), .in1(ULASaida_2_q), .out(Entrada_B_Reg), .sel(MemParaReg));

  assign PC_Jump[2:0] = Funct;

  // Other names for the same wires on the sheet: RD[2:0] = PC_Jump[5:3]; RS[1:0] = PC_Jump[7:6]; ZeroUla = out_9

  // Notes on the sheet:
  //   EscMem: pull=down
  //   RegDst: pull=down
  //   ClearReg: pull=down
  //   ClearData: pull=down
  //   MemParaReg: pull=down
  //   Instrução: pull=down
  //   Endereço: pull=down
  //   ControleUla: pull=down
  //   UlaFonte: pull=down
  //   OPCODE: pull=down
  //   Funct: pull=down
  //   Clear: pull=down
  //   contents of rom_1 (hex, n*v repeats v):
  //   b044 b0cb 4041 20 8603 520 65a 2004 f10c
endmodule
